# Fritzing sketch pdm_fritzing (saved by Fritzing 0.9.3b)
breadboards: 1

parts:
  부품2 = Adafruit Feather M0 WINC1500 [part_number="Adafruit #3010"]
  부품3 = Adafruit PDM Mic [part_number="Adafruit #3492"]

nets:
  N1: 부품2.D1, 부품3.CLK
  GND: 부품2.GND, 부품3.GND
  +3V3: 부품2.+3V3, 부품3.VDD
  N2: 부품2.D9, 부품3.DATA

custom parts:
  Adafruit Feather M0 WINC1500: This is the Adafruit Feather M0 WiFi w/ATWINC1500 - our take on an 'all-in-one' Arduino-compatible + high speed, reliable WiFi with built in USB and battery charging. Its an Adafruit Feather M0 with a WiFi module, ready to rock! Connect your Feather to the Internet with this fine new FCC-certified WiFi module from Atmel. This 802.11bgn-capable WiFi module is the best new thing for networking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
  Adafruit PDM Mic: An exotic new microphone has arrived in the Adafruit shop, a PDM MEMS Microphone! PDM is the 'third' kind of microphone you can integrate with electronics, apart from analog or I2S. These microphones are very commonly used in products, but are rarely seen in maker projects. Still, they have some benefits so we thought we'd offer a breakout for the shop. The first thing to note is that this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
